// Logisim project KrajcovicPPI03.circ as structural Verilog: 1 circuit, main circuit main
module main (
  input  X,
  input  Reset,
  output Y
);

  wire CLK_out, nand_1_out, nand_2_out, nand_3_out, nand_4_out, nand_6_out, nand_7_out, nand_8_out, Z1_q,
       Z2_q, Z2_qn, Z3_q;

  Clock CLK (.out(CLK_out));
  nand nand_1 (nand_1_out, X, X);
  nand nand_2 (nand_2_out, nand_1_out, Z1_q, Z3_q);
  nand nand_3 (nand_3_out, nand_1_out, Z2_q, Z3_q);
  nand nand_4 (nand_4_out, X, Z2_qn, Z3_q);
  nand nand_5 (Y, nand_2_out, nand_2_out);
  nand nand_6 (nand_6_out, nand_3_out, nand_3_out);
  nand nand_7 (nand_7_out, X, nand_4_out);
  nand nand_8 (nand_8_out, nand_4_out, nand_4_out);
  J_K_Flip_Flop Z1 (.J(nand_6_out), .clk(CLK_out), .K(nand_7_out), .Q(Z1_q), .reset(Reset));  // open: Qn, preset, en
  J_K_Flip_Flop Z2 (
    .J(nand_8_out), .clk(CLK_out), .K(nand_1_out), .Q(Z2_q), .Qn(Z2_qn), .reset(Reset));  // open: preset, en
  J_K_Flip_Flop Z3 (.J(X), .clk(CLK_out), .K(nand_7_out), .Q(Z3_q), .reset(Reset));  // open: Qn, preset, en
endmodule
